# Fritzing sketch DS18B20 (saved by Fritzing 0.7.7b)

parts:
  Arduino_Uno_and_Ethernet_shield = Arduino
  R1 = Resistor [tolerance=±5% resistance=4.7k package=THT]
  T2 = DS18B20 Temperature Sensor [part_number=DS18B20 package="TO92 [THT]"]

nets:
  N1: Arduino_Uno_and_Ethernet_shield.D2, R1.Pin_0, T2.DQ
  N2: Arduino_Uno_and_Ethernet_shield.+5V, R1.Pin_1, T2.+Vdd
  GND: Arduino_Uno_and_Ethernet_shield.GND, T2.GND

custom parts:
  DS18B20 Temperature Sensor: A DS18B20 temperature sensor
