# Fritzing sketch LM35 (saved by Fritzing 0.7.7b)

parts:
  Arduino_Uno_and_Ethernet_shield = Arduino
  T1_LM35DZ = LM35 Temperature Sensor [package="TO92 [THT]"]
  C1 = Electrolytic Capacitor [capacitance=10µF voltage=10V package="100 mil [THT, electrolytic]"]

nets:
  N1: Arduino_Uno_and_Ethernet_shield.+5V, T1_LM35DZ.+Vs
  GND: Arduino_Uno_and_Ethernet_shield.GND, T1_LM35DZ.GND, C1.-
  N2: Arduino_Uno_and_Ethernet_shield.A2, T1_LM35DZ.Vout, C1.+
